# Fritzing sketch Self Balancing Robot Fritzing (saved by Fritzing 1.0.4)

parts:
  A1 = ESP32 38Pin narrow
  Part1 = InvenSense MPU6050
  M1 = gear-motor
  M2 = gear-motor
  VCC1 = Battery
  U1 = LM2596 step down module
  A2 = Motor driver tzt DRV8833

nets (from the breadboard view):
  N1: A1.Pin_1, Part1.VCC
  N2: A1.Pin_9, A2.Pin_12
  N3: A1.Pin_10, A2.Pin_11
  N4: A1.Pin_11, A2.Pin_8
  N5: A1.Pin_13, A2.Pin_7
  N6: A1.Pin_14, A1.Pin_38, VCC1.-, U1.IN-, U1.OUT-
  N7: A1.Pin_19, U1.OUT+
  N8: A1.Pin_31, Part1.GND
  N9: A1.Pin_33, Part1.SDA
  N10: A1.Pin_36, Part1.SCL
  N11: M1.pin_1, A2.Pin_4
  N12: M1.pin_2, A2.Pin_5
  N13: M2.pin_1, A2.Pin_2
  N14: M2.pin_2, A2.Pin_3
  N15: VCC1.+, U1.IN+

custom parts:
  ESP32 38Pin narrow: ESP32 38Pin narrow.
  Battery: Your standard 2x 18650 battery pack (7,4 Volts)
  LM2596 step down module: LM2596 DC-DC step down power supply module 3 A.
  Motor driver tzt DRV8833: TZT DRV8833 DC3V-10V 1.5A 2 Channel DC Motor Drive Module.
